# Fritzing sketch buff_board_final (saved by Fritzing 0.8.7b)
circuit board: 7.6cm x 3.9cm
breadboards: 1

parts:
  J1(out) = Screw terminal - 2 pins [package=THT]
  J3(out) = Screw terminal - 2 pins [package=THT]
  J4(out) = Screw terminal - 2 pins [package=THT]
  R1 = Resistor [tolerance=±5% resistance=220 package=THT]
  R2 = Resistor [tolerance=±5% resistance=220 package=THT]
  J2(out) = Screw terminal - 2 pins [package=THT]
  R3 = Resistor [tolerance=±5% resistance=220 package=THT]
  R4 = Resistor [tolerance=±5% resistance=220 package=THT]
  R6 = Resistor [tolerance=±5% resistance=220 package=THT]
  R5 = Resistor [tolerance=±5% resistance=220 package=THT]
  R8 = Resistor [tolerance=±5% resistance=220 package=THT]
  R7 = Resistor [tolerance=±5% resistance=220 package=THT]
  5V = Screw terminal - 2 pins [package=THT]
  IC1 = IC, DIP package, 8 pins [chip_label=IC]
  IC2 = IC, DIP package, 8 pins [chip_label=IC]
  J1(in) = Screw terminal - 2 pins [package=THT]
  J2(in) = Screw terminal - 2 pins [package=THT]
  J4(in) = Screw terminal - 2 pins [package=THT]
  J3(in) = Screw terminal - 2 pins [package=THT]
  R9 = Resistor [tolerance=±5% resistance=220 package=THT]
  IC3 = IC, DIP package, 8 pins [chip_label=IC]
  IC4 = IC, DIP package, 8 pins [chip_label=IC]
  D1 = Diode [package=diode-1n4001]
  D2 = Diode [package=diode-1n4001]
  D3 = Diode [package=diode-1n4001]
  D4 = Diode [package=diode-1n4001]
  D6 = Diode [package=diode-1n4001]
  D5 = Diode [package=diode-1n4001]
  D8 = Diode [package=diode-1n4001]
  D7 = Diode [package=diode-1n4001]
  LED = LED - 3mm [color="Red (633nm)" package="3 mm [THT]"]
  D9 = Diode [package=diode-1n4001]
  C1 = Ceramic Capacitor [capacitance=100nF package="100 mil [THT, multilayer]"]

nets:
  N1: J1(out).pin1, R2.Pin_0, IC1.pin6, D1.C
  N2: J1(out).pin2, R1.Pin_0, IC1.pin3, D2.C
  N3: J3(out).pin1, R5.Pin_0, IC3.pin6, D6.C
  N4: J3(out).pin2, R6.Pin_0, IC3.pin3, D5.C
  N5: J4(out).pin1, R7.Pin_0, IC4.pin6, D8.C
  N6: J4(out).pin2, R8.Pin_0, IC4.pin3, D7.C
  5V: R1.Pin_1, R2.Pin_1, R3.Pin_1, R4.Pin_1, R6.Pin_1, R5.Pin_1, R8.Pin_1, R7.Pin_1, 5V.pin1, IC1.pin8, IC2.pin8, IC3.pin8, IC4.pin8, LED.anode, D9.C, C1.1
  N7: J2(out).pin1, R4.Pin_0, IC2.pin6, D3.C
  N8: J2(out).pin2, R3.Pin_0, IC2.pin3, D4.C
  GND: 5V.pin2, IC1.pin4, IC2.pin4, R9.Pin_0, IC3.pin4, IC4.pin4, D1.A, D2.A, D3.A, D4.A, D6.A, D5.A, D8.A, D7.A, D9.A, C1.0
  N9: IC1.pin2, J1(in).pin2
  N10: IC1.pin7, J1(in).pin1
  N11: IC2.pin2, J2(in).pin2
  N12: IC2.pin7, J2(in).pin1
  N13: J4(in).pin1, IC4.pin7
  N14: J4(in).pin2, IC4.pin2
  N15: J3(in).pin1, IC3.pin7
  N16: J3(in).pin2, IC3.pin2
  N17: R9.Pin_1, LED.cathode

notes:
  Arnau(OSL)
  May 2014
  Nessie
  Buff PCB
  +
